// Logisim project logic.circ as structural Verilog: 17 circuits, main circuit NOT
module NOT (
  input  in_1,
  output out_2
);

  Transistor transistor_1 (.in(1'b1), .out(out_2), .gate(in_1));
  Transistor #(.\type ("n")) transistor_2 (.in(1'b0), .out(out_2), .gate(in_1));

  // Notes on the sheet:
  //   https://en.wikipedia.org/wiki/Inverter_(logic_gate)#Electronic_implementation
endmodule

module NOR (
  input  in_1,
  input  in_2,
  output out_3
);

  wire transistor_1_out;

  Transistor transistor_1 (.in(1'b1), .out(transistor_1_out), .gate(in_1));
  Transistor transistor_2 (.in(transistor_1_out), .out(out_3), .gate(in_2));
  Transistor #(.\type ("n")) transistor_3 (.in(1'b0), .out(out_3), .gate(in_1));
  Transistor #(.\type ("n")) transistor_4 (.in(1'b0), .out(out_3), .gate(in_2));

  // Notes on the sheet:
  //   https://en.wikipedia.org/wiki/NOR_gate#Implementations
endmodule

module OR (
  input  in_1,
  input  in_2,
  output out_3
);

  wire NOR_out_3;

  NOR NOR (.in_1(in_1), .in_2(in_2), .out_3(NOR_out_3));
  NOT NOT (.in_1(NOR_out_3), .out_2(out_3));
endmodule

module AND (
  input  in_1,
  input  in_2,
  output out_3
);

  wire NOT_2_out_2, NOT_out_2;

  NOT NOT (.in_1(in_1), .out_2(NOT_out_2));
  NOT NOT_2 (.in_1(in_2), .out_2(NOT_2_out_2));
  NOR NOR (.in_1(NOT_out_2), .in_2(NOT_2_out_2), .out_3(out_3));

  // Notes on the sheet:
  //   https://en.wikipedia.org/wiki/AND_gate#Alternatives
endmodule

module NAND (
  input  in_1,
  input  in_2,
  output out_3
);

  wire AND_out_3;

  AND AND (.in_1(in_1), .in_2(in_2), .out_3(AND_out_3));
  NOT NOT (.in_1(AND_out_3), .out_2(out_3));
endmodule

module XOR (
  input  in_1,
  input  in_2,
  output out_3
);

  wire NAND_out_3, OR_out_3;

  NAND NAND (.in_1(in_1), .in_2(in_2), .out_3(NAND_out_3));
  OR OR (.in_1(in_1), .in_2(in_2), .out_3(OR_out_3));
  AND AND (.in_1(NAND_out_3), .in_2(OR_out_3), .out_3(out_3));

  // Notes on the sheet:
  //   Exclusive OR: only true if exactly one of the inputs is true
  //   https://en.wikipedia.org/wiki/XOR_gate#Alternatives
endmodule

module _3_bit_NOR (
  input  in_1,
  input  in_2,
  input  in_3,
  output out_4
);

  wire transistor_2_out, transistor_3_out;

  Transistor #(.\type ("n")) transistor_1 (.in(1'b0), .out(out_4), .gate(in_1));
  Transistor transistor_2 (.in(1'b1), .out(transistor_2_out), .gate(in_1));
  Transistor transistor_3 (.in(transistor_2_out), .out(transistor_3_out), .gate(in_2));
  Transistor transistor_4 (.in(transistor_3_out), .out(out_4), .gate(in_3));
  Transistor #(.\type ("n")) transistor_5 (.in(1'b0), .out(out_4), .gate(in_3));
  Transistor #(.\type ("n")) transistor_6 (.in(1'b0), .out(out_4), .gate(in_2));
endmodule

module _3_bit_AND (
  input  in_1,
  input  in_2,
  input  in_3,
  output out_4
);

  wire NOT_2_out_2, NOT_3_out_2, NOT_out_2;

  NOT NOT (.in_1(in_1), .out_2(NOT_out_2));
  NOT NOT_2 (.in_1(in_2), .out_2(NOT_2_out_2));
  NOT NOT_3 (.in_1(in_3), .out_2(NOT_3_out_2));
  _3_bit_NOR NOR (.in_1(NOT_out_2), .in_2(NOT_2_out_2), .in_3(NOT_3_out_2), .out_4(out_4));
endmodule

module _3_bit_NAND (
  input  in_1,
  input  in_2,
  input  in_3,
  output out_4
);

  wire AND_out_4;

  _3_bit_AND AND (.in_1(in_1), .in_2(in_2), .in_3(in_3), .out_4(AND_out_4));
  NOT NOT (.in_1(AND_out_4), .out_2(out_4));
endmodule

module Adder (
  input  A,
  input  B,
  input  CarryIn,
  output Answer,
  output CarryOut
);

  wire and_1_out, and_2_out, xor_1_out;

  xor xor_1 (xor_1_out, A, B);
  and and_1 (and_1_out, xor_1_out, CarryIn);
  xor xor_2 (Answer, xor_1_out, CarryIn);
  and and_2 (and_2_out, A, B);
  or or_1 (CarryOut, and_1_out, and_2_out);

  // Notes on the sheet:
  //   https://en.wikipedia.org/wiki/Adder_(electronics)#Full_adder
endmodule

module _4_bit_Adder (
  input  [3:0] in_1,
  input  [3:0] in_2,
  input  in_3,
  output out_4,
  output [3:0] out_5
);

  wire adder_2_carryout, adder_3_carryout, adder_4_carryout;

  Adder adder_1 (.CarryOut(out_4), .A(in_1[3]), .B(in_2[3]), .Answer(out_5[3]), .CarryIn(adder_2_carryout));
  Adder adder_2 (.CarryOut(adder_2_carryout), .A(in_1[2]), .B(in_2[2]), .Answer(out_5[2]), .CarryIn(adder_3_carryout));
  Adder adder_3 (.CarryOut(adder_3_carryout), .A(in_1[1]), .B(in_2[1]), .Answer(out_5[1]), .CarryIn(adder_4_carryout));
  Adder adder_4 (.CarryOut(adder_4_carryout), .A(in_1[0]), .B(in_2[0]), .Answer(out_5[0]), .CarryIn(in_3));

  // Notes on the sheet:
  //   https://en.wikipedia.org/wiki/Adder_(electronics)#Adders_supporting_multiple_bits
endmodule

module Flip_flop (
  input  Write,
  input  Data_in,
  output Data_out
);

  wire nand_1_out, nand_2_out, nand_3_out, nand_4_out, nand_6_out;

  nand nand_1 (nand_1_out, nand_4_out, nand_2_out);
  nand nand_2 (nand_2_out, nand_1_out, Write);
  nand nand_3 (nand_3_out, nand_2_out, Write, nand_4_out);
  nand nand_4 (nand_4_out, nand_3_out, Data_in);
  nand nand_5 (Data_out, nand_2_out, nand_6_out);
  nand nand_6 (nand_6_out, Data_out, nand_3_out);

  // Notes on the sheet:
  //   https://en.wikipedia.org/wiki/Flip-flop_(electronics)#Classical_positive-edge-triggered_D_flip-flop
endmodule

module Register_File (
  input  [3:0] Data_In,
  input  [1:0] Address,
  input  Write,
  output [3:0] Data_Out
);

  wire and_1_out, and_2_out, and_3_out, and_4_out, Decoder_out0, Decoder_out1, Decoder_out2, Decoder_out3,
       flip_flop_1_data_out, flip_flop_2_data_out, flip_flop_3_data_out, flip_flop_4_data_out,
       flip_flop_5_data_out, flip_flop_6_data_out, flip_flop_7_data_out, flip_flop_8_data_out,
       flip_flop_9_data_out, flip_flop_10_data_out, flip_flop_11_data_out, flip_flop_12_data_out,
       Word_0_data_out, Word_1_data_out, Word_2_data_out, Word_3_data_out;

  Decoder Decoder (.Input(Address), .Out0(Decoder_out0), .Out1(Decoder_out1), .Out2(Decoder_out2), .Out3(Decoder_out3));
  and and_1 (and_1_out, Decoder_out0, Write);
  and and_2 (and_2_out, Decoder_out1, Write);
  and and_3 (and_3_out, Decoder_out2, Write);
  and and_4 (and_4_out, Decoder_out3, Write);
  Flip_flop flip_flop_1 (.Write(and_1_out), .Data_in(Data_In[3]), .Data_out(flip_flop_1_data_out));
  Flip_flop flip_flop_2 (.Write(and_2_out), .Data_in(Data_In[3]), .Data_out(flip_flop_2_data_out));
  Flip_flop flip_flop_3 (.Write(and_3_out), .Data_in(Data_In[3]), .Data_out(flip_flop_3_data_out));
  Flip_flop flip_flop_4 (.Write(and_4_out), .Data_in(Data_In[3]), .Data_out(flip_flop_4_data_out));
  Multiplexer multiplexer_1 (
    .Select(Address), .In0(flip_flop_1_data_out), .In1(flip_flop_2_data_out), .In2(flip_flop_3_data_out),
    .In3(flip_flop_4_data_out), .Output(Data_Out[3]));
  Flip_flop flip_flop_5 (.Write(and_1_out), .Data_in(Data_In[2]), .Data_out(flip_flop_5_data_out));
  Flip_flop flip_flop_6 (.Write(and_2_out), .Data_in(Data_In[2]), .Data_out(flip_flop_6_data_out));
  Flip_flop flip_flop_7 (.Write(and_3_out), .Data_in(Data_In[2]), .Data_out(flip_flop_7_data_out));
  Flip_flop flip_flop_8 (.Write(and_4_out), .Data_in(Data_In[2]), .Data_out(flip_flop_8_data_out));
  Multiplexer multiplexer_2 (
    .Select(Address), .In0(flip_flop_5_data_out), .In1(flip_flop_6_data_out), .In2(flip_flop_7_data_out),
    .In3(flip_flop_8_data_out), .Output(Data_Out[2]));
  Flip_flop flip_flop_9 (.Write(and_1_out), .Data_in(Data_In[1]), .Data_out(flip_flop_9_data_out));
  Flip_flop flip_flop_10 (.Write(and_2_out), .Data_in(Data_In[1]), .Data_out(flip_flop_10_data_out));
  Flip_flop flip_flop_11 (.Write(and_3_out), .Data_in(Data_In[1]), .Data_out(flip_flop_11_data_out));
  Flip_flop flip_flop_12 (.Write(and_4_out), .Data_in(Data_In[1]), .Data_out(flip_flop_12_data_out));
  Multiplexer multiplexer_3 (
    .Select(Address), .In0(flip_flop_9_data_out), .In1(flip_flop_10_data_out), .In2(flip_flop_11_data_out),
    .In3(flip_flop_12_data_out), .Output(Data_Out[1]));
  Flip_flop Word_0 (.Write(and_1_out), .Data_in(Data_In[0]), .Data_out(Word_0_data_out));
  Flip_flop Word_1 (.Write(and_2_out), .Data_in(Data_In[0]), .Data_out(Word_1_data_out));
  Flip_flop Word_2 (.Write(and_3_out), .Data_in(Data_In[0]), .Data_out(Word_2_data_out));
  Flip_flop Word_3 (.Write(and_4_out), .Data_in(Data_In[0]), .Data_out(Word_3_data_out));
  Multiplexer Multiplexers (
    .Select(Address), .In0(Word_0_data_out), .In1(Word_1_data_out), .In2(Word_2_data_out),
    .In3(Word_3_data_out), .Output(Data_Out[0]));

  // Notes on the sheet:
  //   https://en.wikipedia.org/wiki/Register_file
endmodule

module Decoder (
  input  [1:0] Input,
  output Out0,
  output Out1,
  output Out2,
  output Out3
);

  wire not_1_out, not_2_out, not_3_out, not_4_out;

  not not_1 (not_1_out, Input[0]);
  and and_1 (Out0, not_1_out, not_3_out);
  not not_2 (not_2_out, Input[1]);
  not not_3 (not_3_out, Input[1]);
  and and_2 (Out1, Input[0], not_2_out);
  not not_4 (not_4_out, Input[0]);
  and and_3 (Out2, not_4_out, Input[1]);
  and and_4 (Out3, Input[0], Input[1]);

  // Notes on the sheet:
  //   https://en.wikipedia.org/wiki/Binary_decoder
endmodule

module Multiplexer (
  input  In0,
  input  In1,
  input  In2,
  input  In3,
  input  [1:0] Select,
  output Output
);

  wire and_1_out, and_2_out, and_3_out, and_4_out, Decoder_out0, Decoder_out1, Decoder_out2, Decoder_out3;

  Decoder Decoder (.Input(Select), .Out0(Decoder_out0), .Out1(Decoder_out1), .Out2(Decoder_out2), .Out3(Decoder_out3));
  and and_1 (and_1_out, In0, Decoder_out0);
  and and_2 (and_2_out, In1, Decoder_out1);
  or or_1 (Output, and_1_out, and_2_out, and_4_out, and_3_out);
  and and_3 (and_3_out, In3, Decoder_out3);
  and and_4 (and_4_out, In2, Decoder_out2);

  // Notes on the sheet:
  //   https://en.wikipedia.org/wiki/Multiplexer
endmodule

module ALU (
  input  [3:0] A,
  input  [3:0] B,
  input  [1:0] Operation,
  output [3:0] Output
);

  wire [3:0] and_1_out, n4_bit_adder_1_out_5, n4_bit_adder_2_out_5, n4_bit_adder_3_out_5, not_1_out, or_1_out;

  _4_bit_Adder u_4_bit_adder_1 (.in_1(A), .in_2(B), .out_5(n4_bit_adder_1_out_5), .in_3(1'b0));  // open: out_4
  assign not_1_out = ~B;  // NOT_Gate not_1, 4 bits wide
  _4_bit_Adder u_4_bit_adder_2 (
    .in_1(not_1_out), .in_2(4'b0001), .out_5(n4_bit_adder_2_out_5), .in_3(1'b0));  // open: out_4
  _4_bit_Adder u_4_bit_adder_3 (
    .in_1(A), .in_2(n4_bit_adder_2_out_5), .out_5(n4_bit_adder_3_out_5), .in_3(1'b0));  // open: out_4
  Multiplexer_part #(.select(2), .width(4)) multiplexer_1 (
    .in0(n4_bit_adder_1_out_5), .in1(n4_bit_adder_3_out_5), .in2(and_1_out), .in3(or_1_out), .out(Output),
    .sel(Operation));  // open: en
  assign and_1_out = A & B;  // AND_Gate and_1, 4 bits wide
  assign or_1_out = A | B;  // OR_Gate or_1, 4 bits wide

  // Notes on the sheet:
  //   Addition
  //   Subtraction
  //   (negates B with
  //   two's compliment)
  //   https://en.wikipedia.org/wiki/Arithmetic_logic_unit
  //   Bitwise AND
  //   Bitwise OR
endmodule

module Complete_CPUs (
);


  // Notes on the sheet:
  //   https://github.com/Theldus/MSW
  //   https://minnie.tuhs.org/CompArch/Tutes/week03.html
  //   https://cs.mcgill.ca/~mxia3/2018/03/15/XYT-CPU-a-8-bit-built-from-scratch-in-Logisim/
endmodule
